// Logisim project 7segDisplay.circ as structural Verilog: 11 circuits, main circuit main
module main (
  input  [3:0] in_1
);

  wire a, a2, a3, b, b2, b3, c, c2, c3, d, d2, d3, e, e2, e3, f, f2, f3, g, g2, g3, RELOJ;
  wire [3:0] counter_1_q, counter_2_q;

  Counter #(.width(4), .max('h9)) counter_1 (.Q(counter_1_q), .clk(RELOJ));  // open: load, D, count, carry, clr
  integrado _7_display_controller (.\input (in_1), .a(a), .b(b), .c(c), .d(d), .e(e), .f(f), .g(g));
  integrado _7_display_controller_2 (.\input (counter_1_q), .a(a2), .b(b2), .c(c2), .d(d2), .e(e2), .f(f2), .g(g2));
  _7_Segment_Display u_7_segment_display_1 (.g(g), .f(f), .a(a), .b(b), .e(e), .d(d), .c(c));  // open: dp
  _7_Segment_Display u_7_segment_display_2 (.g(g2), .f(f2), .a(a2), .b(b2), .e(e2), .d(d2), .c(c2));  // open: dp
  integrado _7_display_controller_3 (.\input (counter_2_q), .a(a3), .b(b3), .c(c3), .d(d3), .e(e3), .f(f3), .g(g3));
  Counter #(.width(4), .max('h9)) counter_2 (
    .load(1'b1), .count(1'b1), .Q(counter_2_q), .clk(RELOJ));  // open: D, carry, clr
  Clock clock_1 (.out(RELOJ));
  _7_Segment_Display u_7_segment_display_3 (.g(g3), .f(f3), .a(a3), .b(b3), .e(e3), .d(d3), .c(c3));  // open: dp

  // Notes on the sheet:
  //   RICARDO GUEVARA PAYÁN
  //   CIU# 200112036
endmodule

module a (
  input  b0,
  input  b1,
  input  b2,
  input  b3,
  output out_5
);

  wire b1_b3_out, nb0_nb1_nb3_out;

  and b1_b3 (b1_b3_out, b1, b3);
  and nb0_nb1_nb3 (nb0_nb1_nb3_out, ~b1, ~b3);  // AND_Gate
  or or_1 (out_5, b0, b2, b1_b3_out, nb0_nb1_nb3_out);
endmodule

module clock_test (
);

  wire clock_1_out;
  wire [7:0] counter_1_q;

  Counter counter_1 (.Q(counter_1_q), .clk(clock_1_out));  // open: load, D, count, carry, clr
  Clock clock_1 (.out(clock_1_out));
  _7_Segment_Display u_7_segment_display_1 (
    .g(counter_1_q[3]), .f(counter_1_q[2]), .a(counter_1_q[1]), .b(counter_1_q[0]), .e(counter_1_q[4]),
    .d(counter_1_q[5]), .c(counter_1_q[6]), .dp(counter_1_q[7]));
endmodule

module b (
  input  b0,
  input  b1,
  input  b2,
  input  b3,
  output out_5
);

  wire and_1_out, and_2_out;

  and and_1 (and_1_out, ~b2, ~b3);  // AND_Gate
  and and_2 (and_2_out, b2, b3);
  or or_1 (out_5, ~b1, and_1_out, and_2_out);  // OR_Gate
endmodule

module integrado (
  input  [3:0] \input ,
  output a,
  output b,
  output c,
  output d,
  output e,
  output f,
  output g
);

  a a_1 (.b0(\input [3]), .b1(\input [2]), .b2(\input [1]), .b3(\input [0]), .out_5(a));
  d d_1 (.b0(\input [3]), .b1(\input [2]), .b2(\input [1]), .b3(\input [0]), .out_5(d));
  b b_1 (.b0(\input [3]), .b1(\input [2]), .b2(\input [1]), .b3(\input [0]), .out_5(b));
  e e_1 (.b0(\input [3]), .b1(\input [2]), .b2(\input [1]), .b3(\input [0]), .out_5(e));
  c c_1 (.b0(\input [3]), .b1(\input [2]), .b2(\input [1]), .b3(\input [0]), .out_5(c));
  f f_1 (.b0(\input [3]), .b1(\input [2]), .b2(\input [1]), .b3(\input [0]), .out_5(f));
  g g_1 (.b0(\input [3]), .b1(\input [2]), .b2(\input [1]), .b3(\input [0]), .out_5(g));

  // Other names for the same wires on the sheet: d_t = \input [0]; c_t = \input [1]; b_t = \input [2];
  //   a_t = \input [3]
endmodule

module c (
  input  b0,
  input  b1,
  input  b2,
  input  b3,
  output out_5
);

  or or_1 (out_5, b1, ~b2, b3);  // OR_Gate
endmodule

module d (
  input  b0,
  input  b1,
  input  b2,
  input  b3,
  output out_5
);

  wire b1_nb2_b3_out, b2_nb3_out, nb0_nb1_b2_out, nb1_nb3_out;

  and nb1_nb3 (nb1_nb3_out, ~b1, ~b3);  // AND_Gate
  and b2_nb3 (b2_nb3_out, b2, ~b3);  // AND_Gate
  and nb0_nb1_b2 (nb0_nb1_b2_out, ~b0, ~b1, b2);  // AND_Gate
  and b1_nb2_b3 (b1_nb2_b3_out, b1, ~b2, b3);  // AND_Gate
  or or_1 (out_5, b0, nb1_nb3_out, b2_nb3_out, nb0_nb1_b2_out, b1_nb2_b3_out);
endmodule

module e (
  input  b0,
  input  b1,
  input  b2,
  input  b3,
  output out_5
);

  wire b2_nb3_out, nb1_nb3_out;

  and nb1_nb3 (nb1_nb3_out, ~b1, ~b3);  // AND_Gate
  and b2_nb3 (b2_nb3_out, b2, ~b3);  // AND_Gate
  or or_1 (out_5, nb1_nb3_out, b2_nb3_out);
endmodule

module f (
  input  b0,
  input  b1,
  input  b2,
  input  b3,
  output out_5
);

  wire and_1_out, and_2_out, and_3_out;

  and and_1 (and_1_out, b1, ~b2);  // AND_Gate
  and and_2 (and_2_out, b1, ~b3);  // AND_Gate
  and and_3 (and_3_out, ~b2, ~b3);  // AND_Gate
  or or_1 (out_5, b0, and_1_out, and_2_out, and_3_out);
endmodule

module g (
  input  b0,
  input  b1,
  input  b2,
  input  b3,
  output out_5
);

  wire and_1_out, and_2_out, and_3_out;

  and and_1 (and_1_out, b1, ~b2);  // AND_Gate
  and and_2 (and_2_out, b2, ~b3);  // AND_Gate
  and and_3 (and_3_out, ~b0, ~b1, b2);  // AND_Gate
  or or_1 (out_5, b0, and_1_out, and_2_out, and_3_out);
endmodule

module EXTRA (
);

  TTY tty_1 ();  // open: data, clk, we, clr
  Keyboard keyboard_1 ();  // open: clk, re, clr, avail, data
endmodule
