// Logisim project Comparadores.circ as structural Verilog: 4 circuits, main circuit main
module main (
  input  [4:0] A,
  input  [4:0] B,
  output A_B,
  output A_B_2,
  output A_B_3
);

  comparador comparador_1 (.A(A), .B(B), .out_3(A_B), .out_4(A_B_2), .out_5(A_B_3));

  // Notes on the sheet:
  //   Ricardo Guevara
  //   CIU# 200112036
endmodule

module igualdad (
  input  [4:0] A,
  input  [4:0] B,
  output out_3
);

  wire xnor_1_out, xnor_2_out, xnor_3_out, xnor_4_out, xnor_5_out;

  xnor xnor_1 (xnor_1_out, A[0], B[0]);
  xnor xnor_2 (xnor_2_out, A[1], B[1]);
  xnor xnor_3 (xnor_3_out, A[2], B[2]);
  xnor xnor_4 (xnor_4_out, A[3], B[3]);
  xnor xnor_5 (xnor_5_out, A[4], B[4]);
  and and_1 (out_3, xnor_1_out, xnor_2_out, xnor_3_out, xnor_4_out, xnor_5_out);

  // Other names for the same wires on the sheet: a1 = A[0]; a2 = A[1]; a3 = A[2]; a4 = A[3]; a5 = A[4]; b1 = B[0];
  //   b2 = B[1]; b3 = B[2]; b4 = B[3]; b5 = B[4]

  // Notes on the sheet:
  //   A
  //   B
endmodule

module mayor (
  input  [4:0] A,
  input  [4:0] B,
  output resultado
);

  wire a1andnb1, a2andnb2, a2xnorb2, a3andnb3, a3xnorb3, a4andnb4, a4xnorb4, a5andnb5, a5xnorb5, comp1,
       comp2, comp3, comp4;

  and and_1 (a5andnb5, A[4], ~B[4]);  // AND_Gate
  and and_2 (a4andnb4, A[3], ~B[3]);  // AND_Gate
  and and_3 (a3andnb3, A[2], ~B[2]);  // AND_Gate
  and and_4 (a2andnb2, A[1], ~B[1]);  // AND_Gate
  and and_5 (a1andnb1, A[0], ~B[0]);  // AND_Gate
  xnor xnor_1 (a5xnorb5, A[4], B[4]);
  xnor xnor_2 (a4xnorb4, A[3], B[3]);
  xnor xnor_3 (a3xnorb3, A[2], B[2]);
  xnor xnor_4 (a2xnorb2, A[1], B[1]);
  and and_6 (comp1, a5xnorb5, a4andnb4);
  and and_7 (comp2, a5xnorb5, a4xnorb4, a3andnb3);
  and and_8 (comp3, a5xnorb5, a4xnorb4, a3xnorb3, a2andnb2);
  and and_9 (comp4, a5xnorb5, a4xnorb4, a3xnorb3, a2xnorb2, a1andnb1);
  or or_1 (resultado, comp1, comp2, comp3, comp4, a5andnb5);

  // Other names for the same wires on the sheet: a1 = A[0]; a2 = A[1]; a3 = A[2]; a4 = A[3]; a5 = A[4]; b1 = B[0];
  //   b2 = B[1]; b3 = B[2]; b4 = B[3]; b5 = B[4]

  // Notes on the sheet:
  //   A
  //   B
endmodule

module comparador (
  input  [4:0] A,
  input  [4:0] B,
  output out_3,
  output out_4,
  output out_5
);

  mayor mayor_1 (.A(A), .B(B), .resultado(out_3));
  igualdad igualdad_1 (.A(A), .B(B), .out_3(out_4));
  mayor mayor_2 (.A(B), .B(A), .resultado(out_5));
endmodule
