// Logisim project Library.circ as structural Verilog: 3 circuits, main circuit main
module main (
  input  [3:0] in_1,
  input  [4:0] comparador,
  input  [4:0] in_3,
  output out_4,
  output out_5,
  output out_6
);

  wire a, a2, b, b2, c, c2, clock_1_out, d, d2, e, e2, f, f2, g, g2;
  wire [3:0] counter_1_q;

  _7segmentControler u_7segmentcontroler_1 (.\input (in_1), .a(a), .b(b), .c(c), .d(d), .e(e), .f(f), .g(g));
  Comparador comparador_1 (.A(comparador), .B(in_3), .Mayor(out_4), .Igual(out_5), .Menor(out_6));
  _7_Segment_Display u_7_segment_display_1 (.g(g), .f(f), .a(a), .b(b), .e(e), .d(d), .c(c));  // open: dp
  Counter #(.width(4), .max('h9)) counter_1 (
    .load(1'b1), .count(1'b1), .Q(counter_1_q), .clk(clock_1_out));  // open: D, carry, clr
  Clock clock_1 (.out(clock_1_out));
  _7segmentControler u_7segmentcontroler_2 (
    .\input (counter_1_q), .a(a2), .b(b2), .c(c2), .d(d2), .e(e2), .f(f2), .g(g2));
  _7_Segment_Display u_7_segment_display_2 (.g(g2), .f(f2), .a(a2), .b(b2), .e(e2), .d(d2), .c(c2));  // open: dp

  // Notes on the sheet:
  //   7 segment display
endmodule

module Comparador (
  input  [4:0] A,
  input  [4:0] B,
  output Mayor,
  output Igual,
  output Menor
);

  wire a1andnb1, a1xnorb1, a2andnb2, a2xnorb2, a3andnb3, a3xnorb3, a4andnb4, a4xnorb4, a5andnb5, a5xnorb5,
       comp1, comp2, comp3, comp4;

  and and_1 (comp1, a5xnorb5, a4andnb4);
  and and_2 (comp3, a5xnorb5, a4xnorb4, a3xnorb3, a2andnb2);
  and and_3 (a5andnb5, A[4], ~B[4]);  // AND_Gate
  and and_4 (a4andnb4, A[3], ~B[3]);  // AND_Gate
  and and_5 (a3andnb3, A[2], ~B[2]);  // AND_Gate
  and and_6 (a2andnb2, A[1], ~B[1]);  // AND_Gate
  and and_7 (a1andnb1, A[0], ~B[0]);  // AND_Gate
  xnor xnor_1 (a5xnorb5, A[4], B[4]);
  xnor xnor_2 (a4xnorb4, A[3], B[3]);
  xnor xnor_3 (a3xnorb3, A[2], B[2]);
  xnor xnor_4 (a2xnorb2, A[1], B[1]);
  xnor xnor_5 (a1xnorb1, A[0], B[0]);
  and and_8 (comp2, a5xnorb5, a4xnorb4, a3andnb3);
  and and_9 (comp4, a5xnorb5, a4xnorb4, a3xnorb3, a2xnorb2, a1andnb1);
  and and_10 (Menor, ~Mayor, ~Igual);  // AND_Gate
  or or_1 (Mayor, comp1, comp2, comp3, comp4, a5andnb5);
  and and_11 (Igual, a5xnorb5, a4xnorb4, a3xnorb3, a2xnorb2, a1xnorb1);

  // Other names for the same wires on the sheet: a1 = A[0]; a2 = A[1]; a3 = A[2]; a4 = A[3]; a5 = A[4]; b1 = B[0];
  //   b2 = B[1]; b3 = B[2]; b4 = B[3]; b5 = B[4]

  // Notes on the sheet:
  //   A
  //   B
endmodule

module _7segmentControler (
  input  [3:0] \input ,
  output a,
  output b,
  output c,
  output d,
  output e,
  output f,
  output g
);

  wire and_3_out, and_4_out, and_5_out, b1_b3_out, b1_nb2_b3_out, b1andnb2, b2andnb3, nb0nb1b2, nb1andnb3,
       nb2andnb3;

  and nb1_nb3 (nb1andnb3, ~\input [2], ~\input [0]);  // AND_Gate
  and and_1 (nb2andnb3, ~\input [1], ~\input [0]);  // AND_Gate
  and b2_nb3 (b2andnb3, \input [1], ~\input [0]);  // AND_Gate
  and nb0_nb1_b2 (nb0nb1b2, ~\input [3], ~\input [2], \input [1]);  // AND_Gate
  and and_2 (b1andnb2, \input [2], ~\input [1]);  // AND_Gate
  and b1_b3 (b1_b3_out, \input [2], \input [0]);
  or or_1 (a, \input [3], \input [1], b1_b3_out, nb1andnb3);
  and b1_nb2_b3 (b1_nb2_b3_out, \input [2], ~\input [1], \input [0]);  // AND_Gate
  and and_3 (and_3_out, \input [2], ~\input [0]);  // AND_Gate
  and and_4 (and_4_out, \input [1], \input [0]);
  or or_2 (f, \input [3], b1andnb2, and_3_out, nb2andnb3);
  or or_3 (b, ~\input [2], nb2andnb3, and_4_out);  // OR_Gate
  or or_4 (d, \input [3], nb1andnb3, b2andnb3, nb0nb1b2, b1_nb2_b3_out);
  and and_5 (and_5_out, \input [1], ~\input [0]);  // AND_Gate
  or or_5 (c, \input [2], ~\input [1], \input [0]);  // OR_Gate
  or or_6 (e, nb1andnb3, b2andnb3);
  or or_7 (g, \input [3], b1andnb2, and_5_out, nb0nb1b2);

  // Other names for the same wires on the sheet: b3 = \input [0]; b2 = \input [1]; b1 = \input [2]; b0 = \input [3]
endmodule
