// Logisim project latch.circ as structural Verilog
module latch (
  input  s,
  input  r,
  output out_3,
  output out_4
);

  nor nor_1 (out_3, s, out_4);
  nor nor_2 (out_4, out_3, r);

  // Other names for the same wires on the sheet: nq = out_4; q = out_3

  // Notes on the sheet:
  //   latch sr
  //   por qué no cambia el hcr en 0,0?
endmodule

module bit_activacion (
  input  s,
  input  a,
  input  r,
  output out_4,
  output out_5
);

  wire nand_1_out, nand_2_out;

  nand nand_1 (nand_1_out, s, a);
  nand nand_2 (nand_2_out, a, r);
  nor nor_1 (out_4, nand_1_out, out_5);
  nor nor_2 (out_5, out_4, nand_2_out);

  // Other names for the same wires on the sheet: nq = out_5; q = out_4

  // Notes on the sheet:
  //   bit de activación
  //   perdida de información?
  //   latch sr
endmodule

module latch_d (
  input  d,
  input  a,
  output out_3,
  output out_4
);

  wire nand_1_out, nand_2_out;

  nand nand_1 (nand_1_out, d, a);
  nand nand_2 (nand_2_out, a, d);
  nor nor_1 (out_3, nand_1_out, out_4);
  nor nor_2 (out_4, out_3, nand_2_out);

  // Other names for the same wires on the sheet: nq = out_4; q = out_3
endmodule
